// Logisim project async.circ as structural Verilog: 2 circuits, main circuit asyncCounter
module asyncCounter (
  input  Count,
  input  Clock,
  input  RES,
  output [7:0] dOUT,
  output [7:0] iOUT
);

  J_K_Flip_Flop j_k_ff_1 (
    .J(Count), .clk(Clock), .K(Count), .Q(dOUT[0]), .Qn(iOUT[0]), .reset(RES));  // open: preset, en
  J_K_Flip_Flop j_k_ff_2 (
    .J(Count), .clk(dOUT[0]), .K(Count), .Q(dOUT[1]), .Qn(iOUT[1]), .reset(RES));  // open: preset, en
  J_K_Flip_Flop j_k_ff_3 (
    .J(Count), .clk(dOUT[1]), .K(Count), .Q(dOUT[2]), .Qn(iOUT[2]), .reset(RES));  // open: preset, en
  J_K_Flip_Flop j_k_ff_4 (
    .J(Count), .clk(dOUT[2]), .K(Count), .Q(dOUT[3]), .Qn(iOUT[3]), .reset(RES));  // open: preset, en
  J_K_Flip_Flop j_k_ff_5 (
    .J(Count), .clk(dOUT[3]), .K(Count), .Q(dOUT[4]), .Qn(iOUT[4]), .reset(RES));  // open: preset, en
  J_K_Flip_Flop j_k_ff_6 (
    .J(Count), .clk(dOUT[4]), .K(Count), .Q(dOUT[5]), .Qn(iOUT[5]), .reset(RES));  // open: preset, en
  J_K_Flip_Flop j_k_ff_7 (
    .J(Count), .clk(dOUT[5]), .K(Count), .Q(dOUT[6]), .Qn(iOUT[6]), .reset(RES));  // open: preset, en
  J_K_Flip_Flop j_k_ff_8 (
    .J(Count), .clk(dOUT[6]), .K(Count), .Q(dOUT[7]), .Qn(iOUT[7]), .reset(RES));  // open: preset, en
endmodule

module syncCounter (
  input  CLK,
  input  CNT,
  input  RES,
  output carry,
  output [7:0] iOUT,
  output [7:0] dOUT
);

  wire and_1_out, and_2_out, and_3_out, and_4_out, and_5_out, and_6_out;

  T_Flip_Flop t_ff_1 (.clk(CLK), .T(CNT), .Q(iOUT[0]), .Qn(dOUT[0]), .reset(RES));  // open: preset, en
  and and_1 (and_1_out, iOUT[0], iOUT[1]);
  T_Flip_Flop t_ff_2 (.clk(CLK), .T(iOUT[0]), .Q(iOUT[1]), .Qn(dOUT[1]), .reset(RES));  // open: preset, en
  T_Flip_Flop t_ff_3 (.clk(CLK), .T(and_1_out), .Q(iOUT[2]), .Qn(dOUT[2]), .reset(RES));  // open: preset, en
  and and_2 (and_2_out, and_1_out, iOUT[2]);
  and and_3 (and_3_out, and_2_out, iOUT[3]);
  T_Flip_Flop t_ff_4 (.clk(CLK), .T(and_2_out), .Q(iOUT[3]), .Qn(dOUT[3]), .reset(RES));  // open: preset, en
  T_Flip_Flop t_ff_5 (.clk(CLK), .T(and_3_out), .Q(iOUT[4]), .Qn(dOUT[4]), .reset(RES));  // open: preset, en
  and and_4 (and_4_out, and_3_out, iOUT[4]);
  and and_5 (and_5_out, and_4_out, iOUT[5]);
  T_Flip_Flop t_ff_6 (.clk(CLK), .T(and_4_out), .Q(iOUT[5]), .Qn(dOUT[5]), .reset(RES));  // open: preset, en
  T_Flip_Flop t_ff_7 (.clk(CLK), .T(and_5_out), .Q(iOUT[6]), .Qn(dOUT[6]), .reset(RES));  // open: preset, en
  and and_6 (and_6_out, and_5_out, iOUT[6]);
  and and_7 (carry, and_6_out, iOUT[7]);
  T_Flip_Flop t_ff_8 (.clk(CLK), .T(and_6_out), .Q(iOUT[7]), .Qn(dOUT[7]), .reset(RES));  // open: preset, en
endmodule
